// Logisim project JojoMemory.circ as structural Verilog: 4 circuits, main circuit main
module main (
);

  wire _0_out, _1_out, _2_out, _3_out, _4_out, _5_out, _6_out, _7_out, _8_out, _9_out, button_2_out,
       button_out, Clock, decoder_1_out0, decoder_1_out1, decoder_1_out2, decoder_1_out3, Enter_out,
       not_1_out, undriven_2, undriven_5, undriven_6, undriven_7;
  wire [1:0] Digit_Selector;
  wire [3:0] D0, D1, D2, D3, undriven, undriven_3, undriven_4, undriven_8;

  Button _1 (.out(_1_out));
  Button _4 (.out(_4_out));
  Button _7 (.out(_7_out));
  Button button (.out(button_out));
  Clock clock_1 (.out(Clock));
  Button _2 (.out(_2_out));
  Button _3 (.out(_3_out));
  Button _5 (.out(_5_out));
  Button _6 (.out(_6_out));
  Button _8 (.out(_8_out));
  Button _9 (.out(_9_out));
  Button _0 (.out(_0_out));
  Button button_2 (.out(button_2_out));
  Button Enter (.out(Enter_out));
  digit_selector u_digit_selector (.L(button_out), .R(button_2_out), .Clock(Clock), .out_4(Digit_Selector));
  number_display number_display (
    ._0(_0_out), ._1(_1_out), ._2(_2_out), ._3(_3_out), ._4(_4_out), ._5(_5_out), ._6(_6_out), ._7(_7_out),
    ._8(_8_out), ._9(_9_out), .Clock(Clock), .in_12(Digit_Selector), .D0(D0), .D1(D1), .D2(D2), .D3(D3));
  Decoder #(.select(2)) decoder_1 (
    .out0(decoder_1_out0), .out1(decoder_1_out1), .out2(decoder_1_out2), .out3(decoder_1_out3),
    .sel(Digit_Selector));  // open: en
  LED led_1 (.in(decoder_1_out3));
  Hex_Digit_Display hex_digit_display_1 (.value(D3));  // open: dp
  Hex_Digit_Display hex_digit_display_2 (.value(undriven));  // open: dp
  not not_1 (not_1_out, undriven_2);
  Hex_Digit_Display hex_digit_display_3 (.value(undriven_3));  // open: dp
  Hex_Digit_Display hex_digit_display_4 (.value(undriven_4));  // open: dp
  LED led_2 (.in(decoder_1_out2));
  Hex_Digit_Display hex_digit_display_5 (.value(D2));  // open: dp
  Hex_Digit_Display hex_digit_display_6 (.value(undriven_8));  // open: dp
  LED Win (.in(undriven_2));
  LED Lose (.in(not_1_out));
  LED Start (.in(undriven_5));
  LED Game (.in(undriven_6));
  LED Wait (.in(undriven_7));
  LED led_3 (.in(decoder_1_out1));
  LED led_4 (.in(decoder_1_out0));
  Hex_Digit_Display hex_digit_display_7 (.value(D1));  // open: dp
  Hex_Digit_Display hex_digit_display_8 (.value(D0));  // open: dp

  // Notes on the sheet:
  //   Inputs
  //   INSERT CIRCUIT HERE
  //   Bulls
  //   Outputs
  //   Lives
  //   Wins
  //   Cows
endmodule

module setup_memory (
  input  [3:0] D0,
  input  [3:0] D1,
  input  [3:0] D2,
  input  [3:0] D3,
  input  [2:0] State,
  input  Enter,
  output [3:0] S0,
  output [3:0] S1,
  output [3:0] S2,
  output [3:0] S3,
  output [2:0] Lives,
  output [3:0] Wins
);

  wire clock_1_out, SaveDigits;
  wire [3:0] controlled_buffer_1_out, controlled_buffer_2_out, controlled_buffer_3_out,
       controlled_buffer_4_out;

  and and_1 (SaveDigits, ~State[0], ~State[1], ~State[2], Enter);  // AND_Gate
  assign controlled_buffer_1_out = SaveDigits ? D0 : 4'bz;  // Controlled_Buffer controlled_buffer_1
  assign controlled_buffer_2_out = SaveDigits ? D1 : 4'bz;  // Controlled_Buffer controlled_buffer_2
  assign controlled_buffer_3_out = SaveDigits ? D2 : 4'bz;  // Controlled_Buffer controlled_buffer_3
  assign controlled_buffer_4_out = SaveDigits ? D3 : 4'bz;  // Controlled_Buffer controlled_buffer_4
  Register #(.width(4)) register_1 (.D(controlled_buffer_1_out), .Q(S0), .clk(clock_1_out));  // open: en, clr
  Register #(.width(4)) register_2 (.D(controlled_buffer_2_out), .Q(S1), .clk(clock_1_out));  // open: en, clr
  Register #(.width(4)) register_3 (.D(controlled_buffer_3_out), .Q(S2), .clk(clock_1_out));  // open: en, clr
  Register #(.width(4)) register_4 (.D(controlled_buffer_4_out), .Q(S3), .clk(clock_1_out));  // open: en, clr
  Clock clock_1 (.out(clock_1_out));
endmodule

module digit_selector (
  input  L,
  input  R,
  input  Clock,
  output [1:0] out_4
);

  wire and_1_out, and_2_out, and_3_out, and_4_out, and_5_out, and_6_out, and_7_out, and_8_out, and_9_out,
       not_1_out, not_2_out, not_3_out, not_4_out, not_5_out, not_6_out, not_7_out, not_8_out, not_9_out,
       not_10_out, not_11_out, not_12_out, not_13_out, not_14_out, or_1_out, or_2_out;

  not not_1 (not_1_out, R);
  not not_2 (not_2_out, L);
  not not_3 (not_3_out, R);
  not not_4 (not_4_out, out_4[1]);
  not not_5 (not_5_out, out_4[0]);
  not not_6 (not_6_out, L);
  not not_7 (not_7_out, out_4[1]);
  not not_8 (not_8_out, out_4[0]);
  not not_9 (not_9_out, R);
  not not_10 (not_10_out, L);
  and and_1 (and_1_out, not_9_out, not_10_out, out_4[0]);
  not not_11 (not_11_out, R);
  and and_2 (and_2_out, not_11_out, L, not_12_out);
  not not_12 (not_12_out, out_4[0]);
  and and_3 (and_3_out, R, not_13_out, not_14_out);
  not not_13 (not_13_out, L);
  not not_14 (not_14_out, out_4[0]);
  and and_4 (and_4_out, R, L, out_4[0]);
  and and_5 (and_5_out, not_1_out, not_2_out, out_4[1]);
  and and_6 (and_6_out, not_3_out, L, not_4_out, out_4[0]);
  and and_7 (and_7_out, L, out_4[1], not_5_out);
  and and_8 (and_8_out, R, not_6_out, not_7_out, not_8_out);
  and and_9 (and_9_out, R, out_4[1], out_4[0]);
  or or_1 (or_1_out, and_1_out, and_2_out, and_3_out, and_4_out);
  or or_2 (or_2_out, and_5_out, and_6_out, and_7_out, and_8_out, and_9_out);
  D_Flip_Flop d_ff_1 (.clk(Clock), .D(or_2_out), .Q(out_4[1]));  // open: Qn, preset, en, reset
  D_Flip_Flop d_ff_2 (.clk(Clock), .D(or_1_out), .Q(out_4[0]));  // open: Qn, preset, en, reset
endmodule

module number_display (
  input  _0,
  input  _1,
  input  _2,
  input  _3,
  input  _4,
  input  _5,
  input  _6,
  input  _7,
  input  _8,
  input  _9,
  input  Clock,
  input  [1:0] in_12,
  output [3:0] D0,
  output [3:0] D1,
  output [3:0] D2,
  output [3:0] D3
);

  wire and_1_out, and_2_out, and_3_out, and_4_out, Clock_T, decoder_1_out0, decoder_1_out1, decoder_1_out2,
       decoder_1_out3, priority_encoder_1_gs;
  wire [3:0] controlled_buffer_1_out, controlled_buffer_2_out, controlled_buffer_3_out,
       controlled_buffer_4_out, priority_encoder_1_out;

  Priority_Encoder #(.select(4)) priority_encoder_1 (
    .in0(_0), .in1(_1), .in2(_2), .in3(_3), .in4(_4), .in5(_5), .in6(_6), .in7(_7), .in8(_8), .in9(_9),
    .out(priority_encoder_1_out), .gs(priority_encoder_1_gs));  // open: in10, in11, in12, in13, in14, in15, en_out, en_in
  Clock clock_1 (.out(Clock_T));
  // Probe on priority_encoder_1_out
  assign controlled_buffer_1_out = and_1_out ? priority_encoder_1_out : 4'bz;  // Controlled_Buffer controlled_buffer_1
  assign controlled_buffer_2_out = and_2_out ? priority_encoder_1_out : 4'bz;  // Controlled_Buffer controlled_buffer_2
  assign controlled_buffer_3_out = and_3_out ? priority_encoder_1_out : 4'bz;  // Controlled_Buffer controlled_buffer_3
  assign controlled_buffer_4_out = and_4_out ? priority_encoder_1_out : 4'bz;  // Controlled_Buffer controlled_buffer_4
  Decoder #(.select(2)) decoder_1 (
    .out0(decoder_1_out0), .out1(decoder_1_out1), .out2(decoder_1_out2), .out3(decoder_1_out3), .sel(in_12));  // open: en
  Register #(.width(4)) register_1 (.D(controlled_buffer_1_out), .Q(D0), .clk(Clock_T));  // open: en, clr
  and and_1 (and_1_out, priority_encoder_1_gs, decoder_1_out0);
  Register #(.width(4)) register_2 (.D(controlled_buffer_2_out), .Q(D1), .clk(Clock_T));  // open: en, clr
  and and_2 (and_2_out, priority_encoder_1_gs, decoder_1_out1);
  Register #(.width(4)) register_3 (.D(controlled_buffer_3_out), .Q(D2), .clk(Clock_T));  // open: en, clr
  and and_3 (and_3_out, priority_encoder_1_gs, decoder_1_out2);
  Register #(.width(4)) register_4 (.D(controlled_buffer_4_out), .Q(D3), .clk(Clock_T));  // open: en, clr
  and and_4 (and_4_out, priority_encoder_1_gs, decoder_1_out3);
endmodule
