// Logisim project try_proj1.circ as structural Verilog: 7 circuits, main circuit main
module main (
  input  [3:0] setup_input,
  input  [3:0] game_input,
  input  [3:0] in_3,
  input  [3:0] in_4,
  input  [3:0] in_5,
  input  [3:0] in_6,
  input  [3:0] in_7,
  input  [3:0] in_8,
  input  [2:0] in_9
);

  wire and_2_out, clock, clock_1_out, comparator_1_eq, comparator_2_eq, d_ff_2_q, enter, nand_1_out,
       nor_1_out, nor_2_out, same_digit, state3;
  wire [3:0] Bulls, Bulls_output, Cows, Cows_output, sr1;

  Clock clock_1 (.out(clock_1_out));
  D_Flip_Flop d_ff_1 (.clk(clock_1_out), .D(1'b0), .Q(clock), .preset(enter));  // open: Qn, en, reset
  nor nor_1 (nor_1_out, in_9[0], in_9[1], in_9[2]);
  nor nor_2 (nor_2_out, in_9[2], ~in_9[1], ~in_9[0]);  // NOR_Gate
  Comparator #(.width(4), .mode("unsigned")) comparator_1 (
    .a(Bulls), .b(4'b0100), .eq(comparator_1_eq));  // open: gt, lt
  Comparator #(.width(4), .mode("unsigned")) comparator_2 (
    .a(Cows), .b(4'b0100), .eq(comparator_2_eq));  // open: gt, lt
  and and_1 (state3, nor_2_out, ~same_digit);  // AND_Gate
  nand nand_1 (nand_1_out, comparator_1_eq, comparator_2_eq);
  LED led_1 (.in(same_digit));
  Register #(.width(4)) register_1 (.D(setup_input), .en(nor_1_out), .Q(sr1), .clk(clock));  // open: clr
  Register #(.width(4)) register_2 (.D(in_3), .en(nor_1_out), .Q(sr1), .clk(clock));  // open: clr
  Register #(.width(4)) register_3 (.D(in_5), .en(nor_1_out), .Q(sr1), .clk(clock));  // open: clr
  Register #(.width(4)) register_4 (.D(in_7), .en(nor_1_out), .Q(sr1), .clk(clock));  // open: clr
  D_Flip_Flop d_ff_2 (.clk(clock), .D(state3), .Q(d_ff_2_q));  // open: Qn, preset, en, reset
  Button button_1 (.out(enter));
  assign Bulls_output = and_2_out ? Bulls : 4'bz;  // Controlled_Buffer controlled_buffer_1
  assign Cows_output = and_2_out ? Cows : 4'bz;  // Controlled_Buffer controlled_buffer_2
  and and_2 (and_2_out, nand_1_out, d_ff_2_q);
  Hex_Digit_Display hex_digit_display_1 (.value(Bulls_output));  // open: dp
  Register #(.width(4)) register_5 (.D(game_input), .en(state3), .Q(sr1), .clk(clock));  // open: clr
  Register #(.width(4)) register_6 (.D(in_4), .en(state3), .Q(sr1), .clk(clock));  // open: clr
  Register #(.width(4)) register_7 (.D(in_6), .en(state3), .Q(sr1), .clk(clock));  // open: clr
  Register #(.width(4)) register_8 (.D(in_8), .en(state3), .Q(sr1), .clk(clock));  // open: clr
  Hex_Digit_Display hex_digit_display_2 (.value(Cows_output));  // open: dp
  same_digit same_digit_1 (.t1(game_input), .t2(in_4), .t3(in_6), .t4(in_8), .same_digit(same_digit));  // open: state
  bulls_with_display_toggle_and_samedigit_detector bulls_with_display_toggle_and_samedigit_detector_1 (
    .tr1(sr1), .tr2(sr1), .tr3(sr1), .tr4(sr1), .sr1(sr1), .sr2(sr1), .sr3(sr1), .sr4(sr1), .Bulls(Bulls));  // open: state, match
  cows_with_display_toggle_and_samedigit_detector cows_with_display_toggle_and_samedigit_detector_1 (
    .tr1(sr1), .tr2(sr1), .tr3(sr1), .tr4(sr1), .sr1(sr1), .sr2(sr1), .sr3(sr1), .sr4(sr1), .Cows(Cows));  // open: state

  // Other names for the same wires on the sheet: s1[3:0] = setup_input; s2[3:0] = in_3; s3[3:0] = in_5;
  //   s4[3:0] = in_7; state[2:0] = in_9; t1[3:0] = game_input; t2[3:0] = in_4; t3[3:0] = in_6; t4[3:0] = in_8;
  //   sr2[3:0] = sr1; sr3[3:0] = sr1; sr4[3:0] = sr1; tr1[3:0] = sr1; tr2[3:0] = sr1; tr3[3:0] = sr1; tr4[3:0] = sr1
endmodule

module bulls_with_display_toggle_and_samedigit_detector (
  input  [3:0] tr1,
  input  [3:0] tr2,
  input  [3:0] tr3,
  input  [3:0] tr4,
  input  [3:0] sr1,
  input  [3:0] sr2,
  input  [3:0] sr3,
  input  [3:0] sr4,
  input  [2:0] state,
  output [3:0] Bulls,
  output match
);

  wire and_1_out, and_2_out, and_3_out, comparator_1_eq, comparator_2_eq, comparator_3_eq, comparator_4_eq,
       d_ff_1_q;
  wire [2:0] bitadder_1_out;
  wire [3:0] bit_extender_1_out;

  Comparator #(.width(4)) comparator_1 (.a(sr1), .b(tr1), .eq(comparator_1_eq));  // open: gt, lt
  Comparator #(.width(4)) comparator_2 (.a(sr2), .b(tr2), .eq(comparator_2_eq));  // open: gt, lt
  Comparator #(.width(4)) comparator_3 (.a(sr3), .b(tr3), .eq(comparator_3_eq));  // open: gt, lt
  Comparator #(.width(4)) comparator_4 (.a(sr4), .b(tr4), .eq(comparator_4_eq));  // open: gt, lt
  BitAdder #(.width(1)) bitadder_1 (
    .in0(comparator_1_eq), .in1(comparator_2_eq), .in2(comparator_3_eq), .in3(comparator_4_eq),
    .out(bitadder_1_out));
  assign bit_extender_1_out = {{1{1'b0}}, bitadder_1_out};  // Bit_Extender bit_extender_1
  Comparator #(.width(4)) comparator_5 (.a(bit_extender_1_out), .b(4'b0100), .eq(match));  // open: gt, lt
  assign Bulls = and_1_out ? bit_extender_1_out : 4'bz;  // Controlled_Buffer controlled_buffer_1
  and and_1 (and_1_out, and_3_out, d_ff_1_q);
  D_Flip_Flop d_ff_1 (.Q(d_ff_1_q), .preset(and_2_out));  // open: clk, D, Qn, en, reset
  and and_2 (and_2_out, state[2], ~state[1], ~state[0]);  // AND_Gate
  and and_3 (and_3_out, ~state[2], state[1], state[0]);  // AND_Gate
endmodule

module cows_with_display_toggle_and_samedigit_detector (
  input  [3:0] tr1,
  input  [3:0] tr2,
  input  [3:0] tr3,
  input  [3:0] tr4,
  input  [3:0] sr1,
  input  [3:0] sr2,
  input  [3:0] sr3,
  input  [3:0] sr4,
  input  [2:0] state,
  output [3:0] Cows
);

  wire and_1_out, and_2_out, and_3_out, comparator_1_eq, comparator_2_eq, comparator_3_eq, comparator_4_eq,
       comparator_5_eq, comparator_6_eq, comparator_7_eq, comparator_8_eq, comparator_9_eq, comparator_10_eq,
       comparator_11_eq, comparator_12_eq, d_ff_1_q, or_1_out, or_2_out, or_3_out, or_4_out;
  wire [2:0] bitadder_1_out;
  wire [3:0] bit_extender_1_out;

  Comparator #(.width(4)) comparator_1 (.a(tr1), .b(sr2), .eq(comparator_1_eq));  // open: gt, lt
  Comparator #(.width(4)) comparator_2 (.a(tr2), .b(sr1), .eq(comparator_2_eq));  // open: gt, lt
  Comparator #(.width(4)) comparator_3 (.a(tr3), .b(sr1), .eq(comparator_3_eq));  // open: gt, lt
  Comparator #(.width(4)) comparator_4 (.a(tr4), .b(sr1), .eq(comparator_4_eq));  // open: gt, lt
  Comparator #(.width(4)) comparator_5 (.a(tr1), .b(sr3), .eq(comparator_5_eq));  // open: gt, lt
  Comparator #(.width(4)) comparator_6 (.a(tr2), .b(sr3), .eq(comparator_6_eq));  // open: gt, lt
  Comparator #(.width(4)) comparator_7 (.a(tr3), .b(sr2), .eq(comparator_7_eq));  // open: gt, lt
  Comparator #(.width(4)) comparator_8 (.a(tr4), .b(sr2), .eq(comparator_8_eq));  // open: gt, lt
  Comparator #(.width(4)) comparator_9 (.a(tr4), .b(sr3), .eq(comparator_9_eq));  // open: gt, lt
  Comparator #(.width(4)) comparator_10 (.a(tr1), .b(sr4), .eq(comparator_10_eq));  // open: gt, lt
  Comparator #(.width(4)) comparator_11 (.a(tr2), .b(sr4), .eq(comparator_11_eq));  // open: gt, lt
  Comparator #(.width(4)) comparator_12 (.a(tr3), .b(sr4), .eq(comparator_12_eq));  // open: gt, lt
  or or_1 (or_1_out, comparator_4_eq, comparator_8_eq, comparator_9_eq);
  or or_2 (or_2_out, comparator_1_eq, comparator_5_eq, comparator_10_eq);
  or or_3 (or_3_out, comparator_2_eq, comparator_6_eq, comparator_11_eq);
  or or_4 (or_4_out, comparator_3_eq, comparator_7_eq, comparator_12_eq);
  assign bit_extender_1_out = {{1{1'b0}}, bitadder_1_out};  // Bit_Extender bit_extender_1
  BitAdder #(.width(1)) bitadder_1 (
    .in0(or_2_out), .in1(or_3_out), .in2(or_4_out), .in3(or_1_out), .out(bitadder_1_out));
  assign Cows = and_1_out ? bit_extender_1_out : 4'bz;  // Controlled_Buffer controlled_buffer_1
  and and_1 (and_1_out, and_3_out, d_ff_1_q);
  D_Flip_Flop d_ff_1 (.Q(d_ff_1_q), .preset(and_2_out));  // open: clk, D, Qn, en, reset
  and and_2 (and_2_out, state[2], ~state[1], ~state[0]);  // AND_Gate
  and and_3 (and_3_out, ~state[2], state[1], state[0]);  // AND_Gate
endmodule

module same_digit (
  input  [3:0] t1,
  input  [3:0] t2,
  input  [3:0] t3,
  input  [3:0] t4,
  input  [2:0] state,
  output same_digit
);

  wire and_1_out, and_2_out, comparator_1_eq, comparator_2_eq, comparator_3_eq, comparator_4_eq,
       comparator_5_eq, comparator_6_eq, comparator_7_eq, comparator_8_eq, comparator_9_eq, comparator_10_eq,
       comparator_11_eq, comparator_12_eq, or_1_out, or_2_out;

  Comparator #(.width(4)) comparator_1 (.a(t1), .b(t2), .eq(comparator_1_eq));  // open: gt, lt
  Comparator #(.width(4)) comparator_2 (.a(t2), .b(t1), .eq(comparator_2_eq));  // open: gt, lt
  Comparator #(.width(4)) comparator_3 (.a(t3), .b(t1), .eq(comparator_3_eq));  // open: gt, lt
  Comparator #(.width(4)) comparator_4 (.a(t4), .b(t1), .eq(comparator_4_eq));  // open: gt, lt
  Comparator #(.width(4)) comparator_5 (.a(t1), .b(t3), .eq(comparator_5_eq));  // open: gt, lt
  Comparator #(.width(4)) comparator_6 (.a(t2), .b(t3), .eq(comparator_6_eq));  // open: gt, lt
  Comparator #(.width(4)) comparator_7 (.a(t3), .b(t2), .eq(comparator_7_eq));  // open: gt, lt
  Comparator #(.width(4)) comparator_8 (.a(t4), .b(t2), .eq(comparator_8_eq));  // open: gt, lt
  Comparator #(.width(4)) comparator_9 (.a(t1), .b(t4), .eq(comparator_9_eq));  // open: gt, lt
  Comparator #(.width(4)) comparator_10 (.a(t2), .b(t4), .eq(comparator_10_eq));  // open: gt, lt
  Comparator #(.width(4)) comparator_11 (.a(t3), .b(t4), .eq(comparator_11_eq));  // open: gt, lt
  Comparator #(.width(4)) comparator_12 (.a(t4), .b(t3), .eq(comparator_12_eq));  // open: gt, lt
  or or_1 (or_1_out, comparator_1_eq, comparator_5_eq, comparator_9_eq, comparator_2_eq, comparator_6_eq, comparator_10_eq, comparator_3_eq, comparator_7_eq, comparator_11_eq, comparator_4_eq, comparator_8_eq, comparator_12_eq);
  assign same_digit = or_2_out ? or_1_out : 1'bz;  // Controlled_Buffer controlled_buffer_1
  or or_2 (or_2_out, and_2_out, and_1_out);
  and and_1 (and_1_out, ~state[2], state[1], state[0]);  // AND_Gate
  and and_2 (and_2_out, ~state[2], ~state[1], ~state[0]);  // AND_Gate
endmodule

module store_memory_with_samedigit__detector (
  input  [3:0] I0,
  input  [3:0] I1,
  input  [3:0] I2,
  input  [3:0] I3,
  input  Enter,
  input  clock,
  input  Error,
  input  [2:0] state,
  output [3:0] s0,
  output [3:0] s1,
  output [3:0] s2,
  output [3:0] s3
);

  wire and_1_out, and_2_out;

  and and_1 (and_1_out, Enter, ~Error);  // AND_Gate
  and and_2 (and_2_out, and_1_out, ~state[2], ~state[1], ~state[0]);  // AND_Gate
  Register #(.width(4)) register_1 (.D(I0), .en(and_2_out), .Q(s0), .clk(clock));  // open: clr
  Register #(.width(4)) register_2 (.D(I1), .en(and_2_out), .Q(s1), .clk(clock));  // open: clr
  Register #(.width(4)) register_3 (.D(I2), .en(and_2_out), .Q(s2), .clk(clock));  // open: clr
  Register #(.width(4)) register_4 (.D(I3), .en(and_2_out), .Q(s3), .clk(clock));  // open: clr
endmodule

module win_lives_memory_with_samedigit_detector (
  input  match,
  input  error,
  input  clock,
  input  [2:0] state,
  output [3:0] wins,
  output [2:0] lives
);

  wire and_1_out, and_2_out, and_3_out, and_4_out;
  wire [2:0] subtractor_1_out;
  wire [3:0] adder_1_out;

  and and_1 (and_1_out, match, ~error);  // AND_Gate
  Adder #(.width(4)) adder_1 (.a(wins), .b(4'b0001), .out(adder_1_out));  // open: cin, cout
  Subtractor #(.width(3)) subtractor_1 (.a(lives), .b(3'b001), .out(subtractor_1_out));  // open: bin, bout
  and and_2 (and_2_out, and_1_out, and_3_out);
  and and_3 (and_3_out, ~state[0], ~state[1], state[2]);  // AND_Gate
  Register #(.width(4)) u_wins (.D(adder_1_out), .en(and_2_out), .Q(wins), .clk(clock));  // open: clr
  and and_4 (and_4_out, ~state[0], ~state[1], ~state[2]);  // AND_Gate
  D_Flip_Flop d_ff_1 (
    .clk(clock), .D(subtractor_1_out[0]), .Q(lives[0]), .preset(and_4_out), .en(and_3_out));  // open: Qn, reset
  D_Flip_Flop d_ff_2 (
    .clk(clock), .D(subtractor_1_out[1]), .Q(lives[1]), .preset(and_4_out), .en(and_3_out));  // open: Qn, reset
  D_Flip_Flop d_ff_3 (
    .clk(clock), .D(subtractor_1_out[2]), .Q(lives[2]), .preset(and_4_out), .en(and_3_out));  // open: Qn, reset
endmodule

module store_memory_with_samedigit_detector_trystage (
  input  [3:0] I0,
  input  [3:0] I1,
  input  [3:0] I2,
  input  [3:0] I3,
  input  Enter,
  input  clock,
  input  Error,
  input  [2:0] state,
  output [3:0] s0,
  output [3:0] s1,
  output [3:0] s2,
  output [3:0] s3
);

  wire and_1_out, and_2_out;

  and and_1 (and_1_out, Enter, ~Error);  // AND_Gate
  and and_2 (and_2_out, and_1_out, ~state[2], state[1], state[0]);  // AND_Gate
  Register #(.width(4)) register_1 (.D(I0), .en(and_2_out), .Q(s0), .clk(clock));  // open: clr
  Register #(.width(4)) register_2 (.D(I1), .en(and_2_out), .Q(s1), .clk(clock));  // open: clr
  Register #(.width(4)) register_3 (.D(I2), .en(and_2_out), .Q(s2), .clk(clock));  // open: clr
  Register #(.width(4)) register_4 (.D(I3), .en(and_2_out), .Q(s3), .clk(clock));  // open: clr
endmodule
